// Digital circuit 1 Bit Adder.dig as structural Verilog
module _1_Bit_Adder (
  input  Cin,
  input  A,
  input  B,
  output S,
  output Cout
);

  wire and_1_out, and_2_out, xor_1_out;

  xor xor_1 (xor_1_out, Cin, A);
  and and_1 (and_1_out, Cin, A);
  and and_2 (and_2_out, xor_1_out, B);
  xor xor_2 (S, xor_1_out, B);
  or or_1 (Cout, and_2_out, and_1_out);
endmodule
