// Digital circuit 16 Bit Adder.dig as structural Verilog
module _16_Bit_Adder (
  input  [15:0] A,
  input  [15:0] B,
  output [15:0] S
);

  wire _1_bit_adder_1_s, _1_bit_adder_2_cout, _1_bit_adder_3_cout, _1_bit_adder_4_cout, _1_bit_adder_5_cout,
       _1_bit_adder_6_cout, _1_bit_adder_7_cout, _1_bit_adder_8_cout, _1_bit_adder_9_cout,
       _1_bit_adder_10_cout, _1_bit_adder_11_cout, _1_bit_adder_12_cout, _1_bit_adder_13_cout,
       _1_bit_adder_14_cout, _1_bit_adder_15_cout;

  _1_Bit_Adder _1_bit_adder_1 (.Cin(1'b0), .A(A[0]), .B(B[0]), .S(_1_bit_adder_1_s), .Cout(S[0]));
  _1_Bit_Adder _1_bit_adder_2 (.Cin(_1_bit_adder_1_s), .A(A[1]), .B(B[1]), .S(S[1]), .Cout(_1_bit_adder_2_cout));
  _1_Bit_Adder _1_bit_adder_3 (.Cin(_1_bit_adder_2_cout), .A(A[2]), .B(B[2]), .S(S[2]), .Cout(_1_bit_adder_3_cout));
  _1_Bit_Adder _1_bit_adder_4 (.Cin(_1_bit_adder_3_cout), .A(A[3]), .B(B[3]), .S(S[3]), .Cout(_1_bit_adder_4_cout));
  _1_Bit_Adder _1_bit_adder_5 (.Cin(_1_bit_adder_4_cout), .A(A[4]), .B(B[4]), .S(S[4]), .Cout(_1_bit_adder_5_cout));
  _1_Bit_Adder _1_bit_adder_6 (.Cin(_1_bit_adder_5_cout), .A(A[5]), .B(B[5]), .S(S[5]), .Cout(_1_bit_adder_6_cout));
  _1_Bit_Adder _1_bit_adder_7 (.Cin(_1_bit_adder_6_cout), .A(A[6]), .B(B[6]), .S(S[6]), .Cout(_1_bit_adder_7_cout));
  _1_Bit_Adder _1_bit_adder_8 (.Cin(_1_bit_adder_7_cout), .A(A[7]), .B(B[7]), .S(S[7]), .Cout(_1_bit_adder_8_cout));
  _1_Bit_Adder _1_bit_adder_9 (.Cin(_1_bit_adder_8_cout), .A(A[8]), .B(B[8]), .S(S[8]), .Cout(_1_bit_adder_9_cout));
  _1_Bit_Adder _1_bit_adder_10 (.Cin(_1_bit_adder_9_cout), .A(A[9]), .B(B[9]), .S(S[9]), .Cout(_1_bit_adder_10_cout));
  _1_Bit_Adder _1_bit_adder_11 (
    .Cin(_1_bit_adder_10_cout), .A(A[10]), .B(B[10]), .S(S[10]), .Cout(_1_bit_adder_11_cout));
  _1_Bit_Adder _1_bit_adder_12 (
    .Cin(_1_bit_adder_11_cout), .A(A[11]), .B(B[11]), .S(S[11]), .Cout(_1_bit_adder_12_cout));
  _1_Bit_Adder _1_bit_adder_13 (
    .Cin(_1_bit_adder_12_cout), .A(A[12]), .B(B[12]), .S(S[12]), .Cout(_1_bit_adder_13_cout));
  _1_Bit_Adder _1_bit_adder_14 (
    .Cin(_1_bit_adder_13_cout), .A(A[13]), .B(B[13]), .S(S[13]), .Cout(_1_bit_adder_14_cout));
  _1_Bit_Adder _1_bit_adder_15 (
    .Cin(_1_bit_adder_14_cout), .A(A[14]), .B(B[14]), .S(S[14]), .Cout(_1_bit_adder_15_cout));
  _1_Bit_Adder _1_bit_adder_16 (.Cin(_1_bit_adder_15_cout), .A(A[15]), .B(B[15]), .S(S[15]));  // open: Cout
endmodule
