// Digital circuit 8 Bit Register.dig as structural Verilog
module _8_Bit_Register (
  input  [7:0] Din,
  input  En,
  input  Rst,
  input  Clk,
  output [7:0] Dout
);

  wire [7:0] and_1_out;
  wire [7:7] not_1_out;

  not not_1 (not_1_out[7], Rst);
  assign and_1_out = Din & {8{not_1_out[7]}};  // And and_1, 8 bits wide
  D_FlipFlop_wEnable d_flipflop_wenable_1 (.En(En), .Din(and_1_out[0]), .Clk(Clk), .Dout(Dout[0]));
  D_FlipFlop_wEnable d_flipflop_wenable_2 (.En(En), .Din(and_1_out[1]), .Clk(Clk), .Dout(Dout[1]));
  D_FlipFlop_wEnable d_flipflop_wenable_3 (.En(En), .Din(and_1_out[2]), .Clk(Clk), .Dout(Dout[2]));
  D_FlipFlop_wEnable d_flipflop_wenable_4 (.En(En), .Din(and_1_out[3]), .Clk(Clk), .Dout(Dout[3]));
  D_FlipFlop_wEnable d_flipflop_wenable_5 (.En(En), .Din(and_1_out[4]), .Clk(Clk), .Dout(Dout[4]));
  D_FlipFlop_wEnable d_flipflop_wenable_6 (.En(En), .Din(and_1_out[5]), .Clk(Clk), .Dout(Dout[5]));
  D_FlipFlop_wEnable d_flipflop_wenable_7 (.En(En), .Din(and_1_out[6]), .Clk(Clk), .Dout(Dout[6]));
  D_FlipFlop_wEnable d_flipflop_wenable_8 (.En(En), .Din(and_1_out[7]), .Clk(Clk), .Dout(Dout[7]));
endmodule
