// Digital circuit Accumulator.dig as structural Verilog
module Accumulator (
  input  Rst,
  input  Clk,
  input  En,
  input  [15:0] Din,
  output [15:0] Dout
);

  wire or_1_out, or_2_out;

  or or_1 (or_1_out, En, Rst);
  or or_2 (or_2_out, En, Rst);
  _8_Bit_Register _8_bit_register_1 (.Din(Din[7:0]), .En(or_1_out), .Rst(Rst), .Clk(Clk), .Dout(Dout[7:0]));
  _8_Bit_Register _8_bit_register_2 (.Din(Din[15:8]), .En(or_2_out), .Rst(Rst), .Clk(Clk), .Dout(Dout[15:8]));
endmodule
