// Digital circuit D FlipFlop wEnable.dig as structural Verilog
module D_FlipFlop_wEnable (
  input  En,
  input  Din,
  input  Clk,
  output Dout
);

  wire multiplexer_1_out;

  Multiplexer multiplexer_1 (.sel(En), .in_0(Dout), .in_1(Din), .out(multiplexer_1_out));
  D_FF d_ff_1 (.D(multiplexer_1_out), .C(Clk), .Q(Dout));  // open: nQ
endmodule
