// Digital circuit Final Circuit.dig as structural Verilog
module Final_Circuit (
  input  [7:0] Data,
  input  [2:0] Addr,
  input  Write,
  input  RF_Rst,
  input  ACC_Rst,
  input  Clock,
  input  ACC_En,
  output [15:0] Result
);

  wire [7:0] register_file_8x8bits_1_dout;
  wire [15:0] _16_bit_adder_1_s;

  Register_File_8x8bits register_file_8x8bits_1 (
    .Clk(Clock), .Rst(RF_Rst), .Write(Write), .Addr(Addr), .Din(Data), .Dout(register_file_8x8bits_1_dout));
  _16_Bit_Adder _16_bit_adder_1 (.A({{8{1'b0}}, register_file_8x8bits_1_dout}), .B(Result), .S(_16_bit_adder_1_s));
  Accumulator accumulator_1 (.Rst(ACC_Rst), .Clk(Clock), .En(ACC_En), .Din(_16_bit_adder_1_s), .Dout(Result));
endmodule
