// Digital circuit Register File 8x8bits.dig as structural Verilog
module Register_File_8x8bits (
  input  Clk,
  input  Rst,
  input  Write,
  input  [2:0] Addr,
  input  [7:0] Din,
  output [7:0] Dout
);

  wire and_1_out, and_2_out, and_3_out, and_4_out, and_5_out, and_6_out, and_7_out, and_8_out,
       decoder_1_out_0, decoder_1_out_1, decoder_1_out_2, decoder_1_out_3, decoder_1_out_4, decoder_1_out_5,
       decoder_1_out_6, decoder_1_out_7, or_1_out, or_2_out, or_3_out, or_4_out, or_5_out, or_6_out,
       or_7_out, or_8_out;
  wire [7:0] _8_bit_register_1_dout, _8_bit_register_2_dout, _8_bit_register_3_dout, _8_bit_register_4_dout,
       _8_bit_register_5_dout, _8_bit_register_6_dout, _8_bit_register_7_dout, _8_bit_register_8_dout;

  Decoder #(.Selector_Bits(3)) decoder_1 (
    .sel(Addr), .out_0(decoder_1_out_0), .out_1(decoder_1_out_1), .out_2(decoder_1_out_2),
    .out_3(decoder_1_out_3), .out_4(decoder_1_out_4), .out_5(decoder_1_out_5), .out_6(decoder_1_out_6),
    .out_7(decoder_1_out_7));
  and and_1 (and_1_out, decoder_1_out_0, Write);
  and and_2 (and_2_out, decoder_1_out_1, Write);
  and and_3 (and_3_out, decoder_1_out_2, Write);
  and and_4 (and_4_out, decoder_1_out_3, Write);
  and and_5 (and_5_out, decoder_1_out_4, Write);
  and and_6 (and_6_out, decoder_1_out_5, Write);
  and and_7 (and_7_out, decoder_1_out_6, Write);
  and and_8 (and_8_out, decoder_1_out_7, Write);
  or or_1 (or_1_out, and_1_out, Rst);
  or or_2 (or_2_out, and_2_out, Rst);
  or or_3 (or_3_out, and_3_out, Rst);
  or or_4 (or_4_out, and_4_out, Rst);
  or or_5 (or_5_out, and_5_out, Rst);
  or or_6 (or_6_out, and_6_out, Rst);
  or or_7 (or_7_out, and_7_out, Rst);
  or or_8 (or_8_out, and_8_out, Rst);
  _8_Bit_Register _8_bit_register_1 (.Din(Din), .En(or_1_out), .Rst(Rst), .Clk(Clk), .Dout(_8_bit_register_1_dout));
  _8_Bit_Register _8_bit_register_2 (.Din(Din), .En(or_2_out), .Rst(Rst), .Clk(Clk), .Dout(_8_bit_register_2_dout));
  _8_Bit_Register _8_bit_register_3 (.Din(Din), .En(or_3_out), .Rst(Rst), .Clk(Clk), .Dout(_8_bit_register_3_dout));
  _8_Bit_Register _8_bit_register_4 (.Din(Din), .En(or_4_out), .Rst(Rst), .Clk(Clk), .Dout(_8_bit_register_4_dout));
  _8_Bit_Register _8_bit_register_5 (.Din(Din), .En(or_5_out), .Rst(Rst), .Clk(Clk), .Dout(_8_bit_register_5_dout));
  _8_Bit_Register _8_bit_register_6 (.Din(Din), .En(or_6_out), .Rst(Rst), .Clk(Clk), .Dout(_8_bit_register_6_dout));
  _8_Bit_Register _8_bit_register_7 (.Din(Din), .En(or_7_out), .Rst(Rst), .Clk(Clk), .Dout(_8_bit_register_7_dout));
  _8_Bit_Register _8_bit_register_8 (.Din(Din), .En(or_8_out), .Rst(Rst), .Clk(Clk), .Dout(_8_bit_register_8_dout));
  Multiplexer #(.Selector_Bits(3), .Bits(8)) multiplexer_1 (
    .sel(Addr), .in_0(_8_bit_register_1_dout), .in_1(_8_bit_register_2_dout), .in_2(_8_bit_register_3_dout),
    .in_3(_8_bit_register_4_dout), .in_4(_8_bit_register_5_dout), .in_5(_8_bit_register_6_dout),
    .in_6(_8_bit_register_7_dout), .in_7(_8_bit_register_8_dout), .out(Dout));
endmodule
